// Digital circuit part_c.dig as structural Verilog
module part_c (
  input  in_0,
  input  in_1,
  input  in_2,
  output out_0
);

  wire fgnfet_1_s, fgnfet_3_s, fgnfet_5_s, fgnfet_7_s, fgpfet_1_s, fgpfet_2_s, fgpfet_3_s, fgpfet_7_d,
       fgpfet_9_d;

  FGPFET fgpfet_1 (.G(in_2), .S(fgpfet_1_s), .D(1'b0));
  FGPFET fgpfet_2 (.G(in_1), .S(fgpfet_2_s), .D(1'b0));
  FGPFET fgpfet_3 (.G(in_2), .S(fgpfet_3_s), .D(1'b0));
  FGPFET fgpfet_4 (.G(in_0), .S(fgpfet_1_s), .D(1'b0));
  FGPFET fgpfet_5 (.G(in_0), .S(fgpfet_2_s), .D(1'b0));
  FGPFET fgpfet_6 (.G(in_1), .S(fgpfet_3_s), .D(1'b0));
  FGNFET fgnfet_1 (.G(in_0), .D(1'b1), .S(fgnfet_1_s));
  FGNFET fgnfet_2 (.G(in_2), .D(fgnfet_1_s), .S(fgpfet_1_s));
  FGNFET fgnfet_3 (.G(in_0), .D(1'b1), .S(fgnfet_3_s));
  FGNFET fgnfet_4 (.G(in_1), .D(fgnfet_3_s), .S(fgpfet_2_s));
  FGNFET fgnfet_5 (.G(in_1), .D(1'b1), .S(fgnfet_5_s));
  FGNFET fgnfet_6 (.G(in_2), .D(fgnfet_5_s), .S(fgpfet_3_s));
  FGNFET fgnfet_7 (.G(fgpfet_1_s), .D(1'b1), .S(fgnfet_7_s));
  FGNFET fgnfet_8 (.G(fgpfet_2_s), .D(1'b1), .S(fgnfet_7_s));
  FGPFET fgpfet_7 (.G(fgpfet_2_s), .S(fgnfet_7_s), .D(fgpfet_7_d));
  FGPFET fgpfet_8 (.G(fgpfet_1_s), .S(fgpfet_7_d), .D(1'b0));
  FGNFET fgnfet_9 (.G(fgnfet_7_s), .D(1'b1), .S(out_0));
  FGNFET fgnfet_10 (.G(fgpfet_3_s), .D(1'b1), .S(out_0));
  FGPFET fgpfet_9 (.G(fgpfet_3_s), .S(out_0), .D(fgpfet_9_d));
  FGPFET fgpfet_10 (.G(fgnfet_7_s), .S(fgpfet_9_d), .D(1'b0));
endmodule

/* Test case part_c_test:
in_0 in_1 in_2 out_0
 0     0    0     0
 0     0    1     0
 0     1    0     0
 0     1    1     1
 1     0    0     0
 1     0    1     1
 1     1    0     1
 1     1    1     1
*/
