// Digital circuit lab2_part2.dig as structural Verilog
module lab2_part2 (
  input  in0,
  input  in1,
  input  in2,
  input  in3,
  output seg_a,
  output seg_f,
  output seg_b,
  output seg_g,
  output seg_e,
  output seg_c,
  output seg_d,
  output seg_dp,
  output sign_a,
  output sign_f,
  output sign_b,
  output sign_g,
  output sign_e,
  output sign_c,
  output sign_d,
  output sign_dp
);

  Seven_Seg seven_seg_1 (.a(1'b0), .b(1'b0), .c(1'b0), .d(1'b0), .e(1'b0), .f(1'b0), .g(sign_g), .dp(1'b0));
  Seven_Seg seven_seg_2 (.a(seg_a), .b(seg_b), .c(seg_c), .d(seg_d), .e(seg_e), .f(seg_f), .g(seg_g), .dp(1'b0));
  LookUpTable a (.in0(in0), .in1(in1), .in2(in2), .in3(in3), .out(seg_a));
  LookUpTable b (.in0(in0), .in1(in1), .in2(in2), .in3(in3), .out(seg_b));
  LookUpTable c (.in0(in0), .in1(in1), .in2(in2), .in3(in3), .out(seg_c));
  LookUpTable d (.in0(in0), .in1(in1), .in2(in2), .in3(in3), .out(seg_d));
  LookUpTable e (.in0(in0), .in1(in1), .in2(in2), .in3(in3), .out(seg_e));
  LookUpTable f (.in0(in0), .in1(in1), .in2(in2), .in3(in3), .out(seg_f));
  LookUpTable g (.in0(in0), .in1(in1), .in2(in2), .in3(in3), .out(seg_g));
  LookUpTable u_sign_g (.in0(in0), .in1(in1), .in2(in2), .in3(in3), .out(sign_g));

  assign seg_dp = 1'b0;
  assign sign_a = 1'b0;
  assign sign_b = 1'b0;
  assign sign_c = 1'b0;
  assign sign_d = 1'b0;
  assign sign_dp = 1'b0;
  assign sign_e = 1'b0;
  assign sign_f = 1'b0;

  // Notes on the sheet:
  //   Interface (do not edit the content inside this box)
  //   Outputs:
  //   Inputs
  //   Sign
  //   Decimal Number
  //   contents of a (hex, n*v repeats v):
  //   1,0,1,1,0,1,1,1,0,1,1,0,4*1
  //   contents of b (hex, n*v repeats v):
  //   5*1,0,a,5*1,0,0,1,1
  //   contents of c (hex, n*v repeats v):
  //   1,1,a,6*1,0,6*1
  //   contents of d (hex, n*v repeats v):
  //   1,0,1,1,0,1,1,8,8,1,1,0,1,1,0,1
  //   contents of e (hex, n*v repeats v):
  //   1,0,1,0,0,0,1,0,0,1,0,0,0,1,0,1
  //   contents of f (hex, n*v repeats v):
  //   1,0,0,0,1,1,1,4*0,1,1,1,0,1
  //   contents of g (hex, n*v repeats v):
  //   0,0,5*1,0,0,5*1,0,1
  //   contents of sign_g (hex, n*v repeats v):
  //   8*0,8*1
endmodule

/* Test case:
in3 in2 in1 in0  sign_a sign_b sign_c sign_d sign_e sign_f sign_g  seg_a seg_b seg_c seg_d seg_e seg_f seg_g
 0   0   0   0    0      0      0      0      0      0      0       1     1     1     1     1     1     0
*/
